# Fritzing sketch android bot (saved by Fritzing 0.9.2b)
breadboards: 1

parts:
  L1 = Solenoid
  U1 = Voltage Regulator - 5V [package="TO220 [THT]"]
  Part1 = Arduino Uno (Rev3)
  IC1 = L293D [package=THT]
  D1 = LTE-302 [package=lte-302]
  D2 = LTE-302 [package=lte-302]
  L2 = Solenoid
  LED1 = smd LED [color="Green (570nm)" package="0603 [SMD]"]
  R1 = Resistor [tolerance=±5% resistance=330 package="1206 [SMD]"]
  U2 = LIPO-1000mAh [package=lipo-1000]
  Part2 = Bluetooth Mate Silver
  Part3 = HY-SRF05 Ultrasonic Rangefinder

nets:
  N1: L1.pin1, IC1.Out_2_(_Controlled_by_Enable_1_)
  N2: L1.pin2, IC1.Out_1_(_Controlled_by_Enable_1_)
  N3: U1.input_voltage, IC1.+Vmotor, IC1.+V, U2.+
  GND: U1.GND, D1.A, D2.C, R1.Pin_1, U2.-, Part2.GND, Part3.GND
  VCC: U1.output_voltage, IC1.Enable_1, IC1.0V, Part2.VCC, Part3.Vcc
  N4: Part1.D9_PWM, IC1.In_1
  N5: Part1.D10_PWM/SS, IC1.In_2
  N6: Part1.D11_PWM/MOSI, Part2.TX_5V
  N7: Part1.D12/MISO, Part2.RX_5V
  N8: Part1.D13/SCK, LED1.cathode
  N9: Part1.D2, Part3.Trig
  N10: Part1.D3_PWM, D1.C, D2.A
  N11: Part1.D4, Part3.Echo
  N12: Part1.D5_PWM, IC1.In_4
  N13: Part1.D6_PWM, IC1.In_3
  N14: IC1.Out_3_(_Controlled_by_Enable_2_), L2.pin1
  N15: IC1.Out_4_(_Controlled_by_Enable_2_), L2.pin2
  N16: LED1.anode, R1.Pin_0
